// Logisim project IT012_LAB01_25520646.circ as structural Verilog: 4 circuits, main circuit Warmup
module Warmup (
  input  A,
  input  B,
  output F
);

  wire not_1_out;

  not not_1 (not_1_out, B);
  and and_1 (F, A, not_1_out);
endmodule

module TN1 (
  input  A,
  input  B,
  input  C,
  output out_4,
  output out_5,
  output XOR3,
  output out_7,
  output NAND3,
  output out_9,
  output out_10,
  output out_11,
  output CHAIN,
  output out_13
);

  wire X_out;

  not not_1 (out_4, A);
  and and_1 (out_5, A, B);
  or or_1 (out_7, A, B);
  nand nand_1 (out_9, A, B);
  nor nor_1 (out_10, A, B);
  xor xor_1 (out_11, A, B);
  xnor xnor_1 (out_13, A, B);
  xor xor_2 (XOR3, A, B, C);
  nand nand_2 (NAND3, A, B, C);
  nand X (X_out, A, B);
  nand nand_3 (CHAIN, X_out, C);
endmodule

module TN2 (
  input  X,
  input  Y,
  input  Z,
  output EQ1,
  output EQ2,
  output EQ3,
  output EQ4,
  output EQ5
);

  wire and_1_out, and_2_out, and_3_out, and_4_out, and_5_out, not_1_out, not_2_out, not_3_out, not_4_out,
       not_5_out, or_1_out, or_2_out, or_3_out, or_4_out, or_5_out, or_6_out;

  and and_1 (and_1_out, Y, Z);
  not not_1 (not_1_out, X);
  and and_2 (and_2_out, X, Y);
  or or_1 (or_1_out, and_1_out, X);
  and and_3 (and_3_out, not_1_out, Y);
  or or_2 (or_2_out, X, Y);
  not not_2 (not_2_out, and_2_out);
  or or_3 (or_3_out, and_3_out, X);
  not not_3 (not_3_out, or_2_out);
  xnor xnor_1 (EQ1, not_3_out, and_4_out);
  xnor xnor_2 (EQ2, not_2_out, and_4_out);
  xnor xnor_3 (EQ3, or_1_out, and_5_out);
  xnor xnor_4 (EQ4, or_3_out, X);
  xnor xnor_5 (EQ5, or_3_out, or_4_out);
  and and_4 (and_4_out, not_4_out, not_5_out);
  not not_4 (not_4_out, X);
  not not_5 (not_5_out, Y);
  and and_5 (and_5_out, or_5_out, or_6_out);
  or or_4 (or_4_out, X, Y);
  or or_5 (or_5_out, X, Y);
  or or_6 (or_6_out, X, Z);
endmodule

module TN3 (
  input  A,
  input  B,
  input  C,
  input  D,
  output F
);

  wire and_1_out, and_2_out, and_3_out, and_4_out, and_5_out, and_6_out, not_1_out, not_2_out, not_3_out,
       not_4_out, not_5_out, not_6_out, not_7_out, not_8_out, not_9_out, not_10_out;

  not not_1 (not_1_out, A);
  not not_2 (not_2_out, C);
  not not_3 (not_3_out, A);
  not not_4 (not_4_out, B);
  not not_5 (not_5_out, A);
  not not_6 (not_6_out, B);
  and and_1 (and_1_out, not_5_out, not_6_out, C, not_7_out);
  not not_7 (not_7_out, D);
  not not_8 (not_8_out, A);
  not not_9 (not_9_out, B);
  and and_2 (and_2_out, not_8_out, not_9_out, C, D);
  and and_3 (and_3_out, not_1_out, B, not_2_out, D);
  and and_4 (and_4_out, not_3_out, B, C, D);
  and and_5 (and_5_out, A, not_4_out, C, D);
  and and_6 (and_6_out, A, B, not_10_out, D);
  not not_10 (not_10_out, C);
  or or_1 (F, and_1_out, and_2_out, and_3_out, and_4_out, and_5_out, and_6_out);
endmodule
